# Fritzing sketch circuito_vaso (saved by Fritzing 0.9.3b)
breadboards: 1

parts:
  J1 = Peltier Element
  Componente1 = Arduino Nano (Rev3.0) (ICSP)
  LED1 = smd LED [color="Red (633nm)" package="1206 [SMD]"]
  LED2 = smd LED [color="Red (633nm)" package="1206 [SMD]"]
  LED3 = smd LED [color="Red (633nm)" package="1206 [SMD]"]
  R1 = Resistor [tolerance=±5% resistance=220 package="0805 [SMD]"]
  R2 = Resistor [tolerance=±5% resistance=220 package="0805 [SMD]"]
  R3 = Resistor [tolerance=±5% resistance=220 package="0805 [SMD]"]
  RHT1 = Humidity and Temperature Sensor RHT03
  R4 = Resistor [tolerance=±5% resistance=220 package="0805 [SMD]"]

nets:
  N1: J1.pin1, Componente1.GND, LED1.cathode, LED2.cathode, LED3.cathode, RHT1.GND_2
  N2: J1.pin2, R4.Pin_0
  N3: Componente1.D4, RHT1.Data-signal
  N4: Componente1.D5, R4.Pin_1
  N5: Componente1.D6, R1.Pin_1
  VIN: Componente1.VIN, RHT1.Vcc
  N6: LED1.anode, LED2.anode, R3.Pin_0
  N7: R1.Pin_0, R2.Pin_1
  N8: R2.Pin_0, R3.Pin_1
